// Logisim project Meow.circ as structural Verilog: 1 circuit, main circuit main
module main (
  output halted,
  output halted_2,
  output halted_3
);

  wire button_1_out, cdm_8e_1_p1, cdm_8e_1_p2, cdm_8e_1_p4, cdm_8e_1_p5, cdm_8e_1_p7, cdm_8e_1_p8,
       cdm_8e_1_p9, CI, code, data, mem, not_1_out, rd_wr_prime;
  wire [7:0] cdm_8e_1_p13, cdm_8e_1_p14, controlled_buffer_2_out;
  wire [15:0] cdm_8e_1_p12;

  // Debugger debugger_1: pin names not known
  // Probe on cdm_8e_1_p1
  // Probe on cdm_8e_1_p2
  Clock clock_1 (.out(CI));
  // Probe on cdm_8e_1_p4
  // Probe on cdm_8e_1_p5
  // Probe on cdm_8e_1_p7
  Button button_1 (.out(button_1_out));
  // Probe on cdm_8e_1_p8
  // CdM_8e cdm_8e_1: pin names not known; wires that end beside it: cdm_8e_1_p1, cdm_8e_1_p2, CI, cdm_8e_1_p4, cdm_8e_1_p5, button_1_out, cdm_8e_1_p7, cdm_8e_1_p8, cdm_8e_1_p9, mem, rd_wr_prime, cdm_8e_1_p12, cdm_8e_1_p13, cdm_8e_1_p14
  assign cdm_8e_1_p14 = rd_wr_prime ? controlled_buffer_2_out : 8'bz;  // Controlled_Buffer controlled_buffer_1
  // UART uart_1: pin names not known
  Decoder decoder_1 (.out0(code), .out1(data), .sel(cdm_8e_1_p9), .en(mem));
  assign controlled_buffer_2_out = not_1_out ? cdm_8e_1_p13 : 8'bz;  // Controlled_Buffer controlled_buffer_2
  not not_1 (not_1_out, rd_wr_prime);
  ROM #(.addrWidth(16)) rom_1 (.addr(cdm_8e_1_p12), .data(controlled_buffer_2_out), .sel(code));
  RAM #(.addrWidth(16)) ram_1 (
    .addr(cdm_8e_1_p12), .data(controlled_buffer_2_out), .sel(data), .clk(CI), .ld(rd_wr_prime));  // open: clr
  Decoder decoder_2 ();  // open: out0, out1, sel, en

  // Notes on the sheet:
  //   contents of rom_1 (hex, n*v repeats v):
  //   d0 11 d6 6 0 d4 c1 c2 c3 3 60 f e0 14 8b d2 32 72 ed 3 ee c d2 1 4e a e0 3 ee ee 1c ee eb c7 c6 c5
  //   d7 d4
endmodule
